// Logisim project Lab4.circ as structural Verilog: 7 circuits, main circuit main
module main (
  input  [31:0] Instruction
);

  wire alu_controler1_1_alu_src, clock_1_out;
  wire [3:0] alu_controler1_1_alu_ctrl0;
  wire [31:0] bit_extender_1_out, multiplexer_1_out, regthreetwo_1_rdata1, regthreetwo_1_rdata2,
       threetwobitalu_1_r;

  Clock clock_1 (.out(clock_1_out));
  assign bit_extender_1_out = {{20{Instruction[31]}}, Instruction[31:20]};  // Bit_Extender bit_extender_1
  RegthreeTwo regthreetwo_1 (
    .WData(threetwobitalu_1_r), .Clock_in(clock_1_out), .Write(1'b1), .WReg(Instruction[11:7]),
    .RReg1(Instruction[19:15]), .RReg2(Instruction[24:20]), .RData1(regthreetwo_1_rdata1),
    .RData2(regthreetwo_1_rdata2));
  Multiplexer #(.enable("false"), .width(32)) multiplexer_1 (
    .in0(regthreetwo_1_rdata2), .in1(bit_extender_1_out), .out(multiplexer_1_out),
    .sel(alu_controler1_1_alu_src));
  ALU_Controler1 alu_controler1_1 (
    .I30(Instruction[30]), .I14(Instruction[14]), .I13(Instruction[13]), .I12(Instruction[12]),
    .I6(Instruction[6]), .I5(Instruction[5]), .I4(Instruction[4]), .ALU_Ctrl3(alu_controler1_1_alu_ctrl0[3]),
    .ALU_Ctrl2(alu_controler1_1_alu_ctrl0[2]), .ALU_Ctrl1(alu_controler1_1_alu_ctrl0[1]),
    .ALU_Ctrl0(alu_controler1_1_alu_ctrl0[0]), .ALU_Src(alu_controler1_1_alu_src));
  ThreeTwoBitALU threetwobitalu_1 (
    .ALUCtrl(alu_controler1_1_alu_ctrl0), .A(regthreetwo_1_rdata1), .B(multiplexer_1_out),
    .R(threetwobitalu_1_r));  // open: Cin, Cout
endmodule

module ALU_Controler1 (
  input  I30,
  input  I14,
  input  I13,
  input  I12,
  input  I6,
  input  I5,
  input  I4,
  output ALU_Ctrl3,
  output ALU_Ctrl2,
  output ALU_Ctrl1,
  output ALU_Ctrl0,
  output ALU_Src
);

  wire and_2_out, not_1_out, not_2_out, not_3_out, not_4_out, not_5_out;

  not not_1 (not_1_out, I14);
  not not_2 (not_2_out, I13);
  not not_3 (not_3_out, I12);
  not not_4 (not_4_out, I5);
  not not_5 (not_5_out, I4);
  and and_1 (ALU_Ctrl2, I30, not_2_out, I5);
  or or_1 (ALU_Ctrl1, not_2_out, not_5_out);
  and and_2 (and_2_out, I13, not_3_out);
  or or_2 (ALU_Src, not_4_out, not_5_out);
  or or_3 (ALU_Ctrl0, not_1_out, and_2_out);

  assign ALU_Ctrl3 = 1'b0;
endmodule

module OneBFA (
  input  A,
  input  B,
  input  Cin,
  output S,
  output Cout
);

  wire and_1_out, and_2_out, and_3_out, and_4_out, and_5_out, and_6_out, and_7_out, not_1_out, not_2_out,
       not_3_out;

  not not_1 (not_1_out, A);
  not not_2 (not_2_out, B);
  not not_3 (not_3_out, Cin);
  and and_1 (and_1_out, not_1_out, not_2_out, Cin);
  and and_2 (and_2_out, not_1_out, B, not_3_out);
  and and_3 (and_3_out, A, not_2_out, not_3_out);
  and and_4 (and_4_out, A, B, Cin);
  and and_5 (and_5_out, B, Cin);
  and and_6 (and_6_out, A, Cin);
  and and_7 (and_7_out, A, B);
  or or_1 (S, and_1_out, and_2_out, and_3_out, and_4_out);
  or or_2 (Cout, and_5_out, and_6_out, and_7_out);
endmodule

module OneBitALU (
  input  [3:0] ALUCtrl,
  input  A,
  input  B,
  input  Cin,
  output R,
  output Cout
);

  wire and_1_out, multiplexer_1_out, not_1_out, onebfa_1_s, or_1_out, xor_1_out;

  not not_1 (not_1_out, B);
  Multiplexer #(.enable("false")) multiplexer_1 (.in0(B), .in1(not_1_out), .out(multiplexer_1_out), .sel(ALUCtrl[2]));
  and and_1 (and_1_out, A, multiplexer_1_out);
  or or_1 (or_1_out, A, multiplexer_1_out);
  xor xor_1 (xor_1_out, A, multiplexer_1_out);
  OneBFA onebfa_1 (.A(A), .B(multiplexer_1_out), .Cin(Cin), .S(onebfa_1_s), .Cout(Cout));
  Multiplexer #(.enable("false"), .select(2)) multiplexer_2 (
    .in0(and_1_out), .in1(or_1_out), .in2(xor_1_out), .in3(onebfa_1_s), .out(R), .sel(ALUCtrl[1:0]));
endmodule

module FourBitALU (
  input  [3:0] ALUCtrl,
  input  [3:0] A,
  input  [3:0] B,
  input  Cin,
  output [3:0] R,
  output Cout
);

  wire onebitalu_1_cout, onebitalu_2_cout, onebitalu_3_cout;

  OneBitALU onebitalu_1 (.ALUCtrl(ALUCtrl), .A(A[0]), .B(B[0]), .Cin(Cin), .R(R[0]), .Cout(onebitalu_1_cout));
  OneBitALU onebitalu_2 (
    .ALUCtrl(ALUCtrl), .A(A[1]), .B(B[1]), .Cin(onebitalu_1_cout), .R(R[1]), .Cout(onebitalu_2_cout));
  OneBitALU onebitalu_3 (
    .ALUCtrl(ALUCtrl), .A(A[2]), .B(B[2]), .Cin(onebitalu_2_cout), .R(R[2]), .Cout(onebitalu_3_cout));
  OneBitALU onebitalu_4 (.ALUCtrl(ALUCtrl), .A(A[3]), .B(B[3]), .Cin(onebitalu_3_cout), .R(R[3]), .Cout(Cout));
endmodule

module ThreeTwoBitALU (
  input  [3:0] ALUCtrl,
  input  [31:0] A,
  input  [31:0] B,
  input  Cin,
  output [31:0] R,
  output Cout
);

  wire fourbitalu_1_cout, fourbitalu_2_cout, fourbitalu_3_cout, fourbitalu_4_cout, fourbitalu_5_cout,
       fourbitalu_6_cout, fourbitalu_7_cout;

  FourBitALU fourbitalu_1 (.ALUCtrl(ALUCtrl), .A(A[3:0]), .B(B[3:0]), .Cin(Cin), .R(R[3:0]), .Cout(fourbitalu_1_cout));
  FourBitALU fourbitalu_2 (
    .ALUCtrl(ALUCtrl), .A(A[7:4]), .B(B[7:4]), .Cin(fourbitalu_1_cout), .R(R[7:4]), .Cout(fourbitalu_2_cout));
  FourBitALU fourbitalu_3 (
    .ALUCtrl(ALUCtrl), .A(A[11:8]), .B(B[11:8]), .Cin(fourbitalu_2_cout), .R(R[11:8]),
    .Cout(fourbitalu_3_cout));
  FourBitALU fourbitalu_4 (
    .ALUCtrl(ALUCtrl), .A(A[15:12]), .B(B[15:12]), .Cin(fourbitalu_3_cout), .R(R[15:12]),
    .Cout(fourbitalu_4_cout));
  FourBitALU fourbitalu_5 (
    .ALUCtrl(ALUCtrl), .A(A[19:16]), .B(B[19:16]), .Cin(fourbitalu_4_cout), .R(R[19:16]),
    .Cout(fourbitalu_5_cout));
  FourBitALU fourbitalu_6 (
    .ALUCtrl(ALUCtrl), .A(A[23:20]), .B(B[23:20]), .Cin(fourbitalu_5_cout), .R(R[23:20]),
    .Cout(fourbitalu_6_cout));
  FourBitALU fourbitalu_7 (
    .ALUCtrl(ALUCtrl), .A(A[27:24]), .B(B[27:24]), .Cin(fourbitalu_6_cout), .R(R[27:24]),
    .Cout(fourbitalu_7_cout));
  FourBitALU fourbitalu_8 (
    .ALUCtrl(ALUCtrl), .A(A[31:28]), .B(B[31:28]), .Cin(fourbitalu_7_cout), .R(R[31:28]), .Cout(Cout));
endmodule

module RegthreeTwo (
  input  [31:0] WData,
  input  Clock_in,
  input  Write,
  input  [4:0] WReg,
  input  [4:0] RReg1,
  input  [4:0] RReg2,
  output [31:0] RData1,
  output [31:0] RData2
);

  wire D1, D2, D3, D4, D5, D6, D7, D8, D9, D10, D11, D12, D13, D14, D15, D16, D17, D18, D19, D20, D21, D22,
       D23, D24, D25, D26, D27, D28, D29, D30, D31, D32, undriven;
  wire [31:0] Q1, Q2, Q3, Q4, Q5, Q6, Q7, Q8, Q9, Q10, Q11, Q12, Q13, Q14, Q15, Q16, Q17, Q18, Q19, Q20, Q21,
       Q22, Q23, Q24, Q25, Q26, Q27, Q28, Q29, Q30, Q31, Q32;

  Demultiplexer #(.enable("false"), .select(5)) demultiplexer_1 (
    .out0(D1), .out1(D2), .out2(D3), .out3(D4), .out4(D5), .out5(D6), .out6(D7), .out7(D8), .out8(D9),
    .out9(D10), .out10(D11), .out11(D12), .out12(D13), .out13(D14), .out14(D15), .out15(D16), .out16(D17),
    .out17(D18), .out18(D19), .out19(D20), .out20(D21), .out21(D22), .out22(D23), .out23(D24), .out24(D25),
    .out25(D26), .out26(D27), .out27(D28), .out28(D29), .out29(D30), .out30(D31), .out31(D32), .in(Write),
    .sel(WReg));
  Register #(.width(32)) register_1 (.D(WData), .en(D1), .clk(Clock_in), .Q(Q1), .clr(Write));
  Register #(.width(32)) register_2 (.D(WData), .en(D2), .clk(Clock_in), .Q(Q2));  // open: clr
  Register #(.width(32)) register_3 (.D(WData), .en(D3), .clk(Clock_in), .Q(Q3));  // open: clr
  Register #(.width(32)) register_4 (.D(WData), .en(D4), .clk(Clock_in), .Q(Q4));  // open: clr
  Register #(.width(32)) register_5 (.D(WData), .en(D5), .clk(Clock_in), .Q(Q5));  // open: clr
  Register #(.width(32)) register_6 (.D(WData), .en(D6), .clk(Clock_in), .Q(Q6), .clr(undriven));
  Register #(.width(32)) register_7 (.D(WData), .en(D6), .clk(Clock_in), .Q(Q6), .clr(undriven));
  Register #(.width(32)) register_8 (.D(WData), .en(D7), .clk(Clock_in), .Q(Q7));  // open: clr
  Register #(.width(32)) register_9 (.D(WData), .en(D8), .clk(Clock_in), .Q(Q8));  // open: clr
  Register #(.width(32)) register_10 (.D(WData), .en(D9), .clk(Clock_in), .Q(Q9));  // open: clr
  Register #(.width(32)) register_11 (.D(WData), .en(D10), .clk(Clock_in), .Q(Q10));  // open: clr
  Register #(.width(32)) register_12 (.D(WData), .en(D11), .clk(Clock_in), .Q(Q11));  // open: clr
  Register #(.width(32)) register_13 (.D(WData), .en(D12), .clk(Clock_in), .Q(Q12));  // open: clr
  Register #(.width(32)) register_14 (.D(WData), .en(D13), .clk(Clock_in), .Q(Q13));  // open: clr
  Register #(.width(32)) register_15 (.D(WData), .en(D14), .clk(Clock_in), .Q(Q14));  // open: clr
  Register #(.width(32)) register_16 (.D(WData), .en(D15), .clk(Clock_in), .Q(Q15));  // open: clr
  Register #(.width(32)) register_17 (.D(WData), .en(D16), .clk(Clock_in), .Q(Q16));  // open: clr
  Register #(.width(32)) register_18 (.D(WData), .en(D17), .clk(Clock_in), .Q(Q17));  // open: clr
  Register #(.width(32)) register_19 (.D(WData), .en(D18), .clk(Clock_in), .Q(Q18));  // open: clr
  Register #(.width(32)) register_20 (.D(WData), .en(D19), .clk(Clock_in), .Q(Q19));  // open: clr
  Register #(.width(32)) register_21 (.D(WData), .en(D20), .clk(Clock_in), .Q(Q20));  // open: clr
  Register #(.width(32)) register_22 (.D(WData), .en(D21), .clk(Clock_in), .Q(Q21));  // open: clr
  Register #(.width(32)) register_23 (.D(WData), .en(D22), .clk(Clock_in), .Q(Q22));  // open: clr
  Register #(.width(32)) register_24 (.D(WData), .en(D23), .clk(Clock_in), .Q(Q23));  // open: clr
  Register #(.width(32)) register_25 (.D(WData), .en(D24), .clk(Clock_in), .Q(Q24));  // open: clr
  Register #(.width(32)) register_26 (.D(WData), .en(D25), .clk(Clock_in), .Q(Q25));  // open: clr
  Register #(.width(32)) register_27 (.D(WData), .en(D26), .clk(Clock_in), .Q(Q26));  // open: clr
  Register #(.width(32)) register_28 (.D(WData), .en(D27), .clk(Clock_in), .Q(Q27));  // open: clr
  Register #(.width(32)) register_29 (.D(WData), .en(D28), .clk(Clock_in), .Q(Q28));  // open: clr
  Register #(.width(32)) register_30 (.D(WData), .en(D29), .clk(Clock_in), .Q(Q29));  // open: clr
  Register #(.width(32)) register_31 (.D(WData), .en(D30), .clk(Clock_in), .Q(Q30));  // open: clr
  Register #(.width(32)) register_32 (.D(WData), .en(D31), .clk(Clock_in), .Q(Q31));  // open: clr
  Register #(.width(32)) register_33 (.D(WData), .en(D32), .clk(Clock_in), .Q(Q32));  // open: clr
  Multiplexer #(.enable("false"), .select(5), .width(32)) multiplexer_1 (
    .in0(Q1), .in1(Q2), .in2(Q3), .in3(Q4), .in4(Q5), .in5(Q6), .in6(Q7), .in7(Q8), .in8(Q9), .in9(Q10),
    .in10(Q11), .in11(Q12), .in12(Q13), .in13(Q14), .in14(Q15), .in15(Q16), .in16(Q17), .in17(Q18),
    .in18(Q19), .in19(Q20), .in20(Q21), .in21(Q22), .in22(Q23), .in23(Q24), .in24(Q25), .in25(Q26),
    .in26(Q27), .in27(Q28), .in28(Q29), .in29(Q30), .in30(Q31), .in31(Q32), .out(RData1), .sel(RReg1));
  Multiplexer #(.enable("false"), .select(5), .width(32)) multiplexer_2 (
    .in0(Q1), .in1(Q2), .in2(Q3), .in3(Q4), .in4(Q5), .in5(Q6), .in6(Q7), .in7(Q8), .in8(Q9), .in9(Q10),
    .in10(Q11), .in11(Q12), .in12(Q13), .in13(Q14), .in14(Q15), .in15(Q16), .in16(Q17), .in17(Q18),
    .in18(Q19), .in19(Q20), .in20(Q21), .in21(Q22), .in22(Q23), .in23(Q24), .in24(Q25), .in25(Q26),
    .in26(Q27), .in27(Q28), .in28(Q29), .in29(Q30), .in30(Q31), .in31(Q32), .out(RData2), .sel(RReg2));
endmodule
